// Logisim project cpu_logisim.circ as structural Verilog
module instruction_fetch (
  input  [15:0] pc_in,
  output [2:0] alu_op
);

  wire [7:0] rom_1_p2;

  // ROM #(.addrWidth(15), .line("quad")) rom_1: pin names not known; wires that end beside it: pc_in[14:0], rom_1_p2
endmodule

module register_file (
  input  we_in_1,
  input  [1:0] in_sel_1,
  input  out_en_1,
  input  [1:0] sel_out_1,
  input  we_in_2,
  input  [1:0] in_sel_2,
  input  out_en_2,
  input  [1:0] sel_out_2,
  input  res,
  output [7:0] output_1,
  output [7:0] output_2
);

  wire clock_1_out, clock_2_out, clock_3_out, clock_4_out, comparator_1_eq, decoder_1_out0, decoder_1_out1,
       decoder_1_out2, decoder_1_out3, decoder_2_out0, decoder_2_out1, decoder_2_out2, decoder_2_out3,
       decoder_3_out0, decoder_3_out1, decoder_3_out2, decoder_3_out3, decoder_4_out0, decoder_4_out1,
       decoder_4_out2, decoder_4_out3, or_1_out, or_2_out, or_3_out, or_4_out;
  wire [7:0] controlled_buffer_1_out, controlled_buffer_3_out, controlled_buffer_5_out,
       controlled_buffer_7_out, register_1_q, register_2_q, register_3_q, register_4_q, undriven, undriven_2;

  Comparator #(.mode("unsigned"), .width(2)) comparator_1 (
    .a(in_sel_1), .b(in_sel_2), .eq(comparator_1_eq));  // open: gt, lt
  Decoder #(.select(2)) decoder_1 (
    .out0(decoder_1_out0), .out1(decoder_1_out1), .out2(decoder_1_out2), .out3(decoder_1_out3),
    .sel(in_sel_1), .en(we_in_1));
  Decoder #(.select(2)) decoder_2 (
    .out0(decoder_2_out0), .out1(decoder_2_out1), .out2(decoder_2_out2), .out3(decoder_2_out3),
    .sel(in_sel_2), .en(we_in_2));
  // AND_Gate and_1 has open pins: in0=comparator_1_eq, in1=we_in_2, in2=we_in_1, out=open
  assign controlled_buffer_1_out = decoder_1_out0 ? undriven : 8'bz;  // Controlled_Buffer controlled_buffer_1
  assign controlled_buffer_1_out = decoder_2_out0 ? undriven_2 : 8'bz;  // Controlled_Buffer controlled_buffer_2
  assign controlled_buffer_3_out = decoder_1_out1 ? undriven : 8'bz;  // Controlled_Buffer controlled_buffer_3
  assign controlled_buffer_3_out = decoder_2_out1 ? undriven_2 : 8'bz;  // Controlled_Buffer controlled_buffer_4
  assign controlled_buffer_5_out = decoder_1_out2 ? undriven : 8'bz;  // Controlled_Buffer controlled_buffer_5
  assign controlled_buffer_5_out = decoder_2_out2 ? undriven_2 : 8'bz;  // Controlled_Buffer controlled_buffer_6
  assign controlled_buffer_7_out = decoder_1_out3 ? undriven : 8'bz;  // Controlled_Buffer controlled_buffer_7
  assign controlled_buffer_7_out = decoder_2_out3 ? undriven_2 : 8'bz;  // Controlled_Buffer controlled_buffer_8
  Register register_1 (.D(controlled_buffer_1_out), .en(or_1_out), .clk(clock_1_out), .Q(register_1_q), .clr(res));
  or or_1 (or_1_out, decoder_1_out0, decoder_2_out0);
  Clock clock_1 (.out(clock_1_out));
  Register register_2 (.D(controlled_buffer_3_out), .en(or_2_out), .clk(clock_2_out), .Q(register_2_q), .clr(res));
  or or_2 (or_2_out, decoder_1_out1, decoder_2_out1);
  Clock clock_2 (.out(clock_2_out));
  Register register_3 (.D(controlled_buffer_5_out), .en(or_3_out), .clk(clock_3_out), .Q(register_3_q), .clr(res));
  or or_3 (or_3_out, decoder_1_out2, decoder_2_out2);
  Clock clock_3 (.out(clock_3_out));
  Register register_4 (.D(controlled_buffer_7_out), .en(or_4_out), .clk(clock_4_out), .Q(register_4_q), .clr(res));
  or or_4 (or_4_out, decoder_1_out3, decoder_2_out3);
  Clock clock_4 (.out(clock_4_out));
  assign output_1 = decoder_3_out0 ? register_1_q : 8'bz;  // Controlled_Buffer controlled_buffer_9
  assign output_2 = decoder_4_out0 ? register_1_q : 8'bz;  // Controlled_Buffer controlled_buffer_10
  assign output_1 = decoder_3_out1 ? register_2_q : 8'bz;  // Controlled_Buffer controlled_buffer_11
  assign output_2 = decoder_4_out1 ? register_2_q : 8'bz;  // Controlled_Buffer controlled_buffer_12
  assign output_1 = decoder_3_out2 ? register_3_q : 8'bz;  // Controlled_Buffer controlled_buffer_13
  assign output_2 = decoder_4_out2 ? register_3_q : 8'bz;  // Controlled_Buffer controlled_buffer_14
  assign output_1 = decoder_3_out3 ? register_4_q : 8'bz;  // Controlled_Buffer controlled_buffer_15
  assign output_2 = decoder_4_out3 ? register_4_q : 8'bz;  // Controlled_Buffer controlled_buffer_16
  Decoder #(.select(2)) decoder_3 (
    .out0(decoder_3_out0), .out1(decoder_3_out1), .out2(decoder_3_out2), .out3(decoder_3_out3),
    .sel(sel_out_1), .en(out_en_1));
  Decoder #(.select(2)) decoder_4 (
    .out0(decoder_4_out0), .out1(decoder_4_out1), .out2(decoder_4_out2), .out3(decoder_4_out3),
    .sel(sel_out_2), .en(out_en_2));
endmodule

module alu (
  input  [3:0] flags_i,
  input  [7:0] input_1,
  input  [7:0] input_2,
  input  [1:0] alu_op,
  input  shift,
  input  singel_operand,
  output flags_o
);

  wire adder_1_cout;
  wire [7:0] adder_1_out, and_1_out, multiplexer_1_out, not_1_out, or_1_out, xor_1_out;

  Adder adder_1 (.a(input_1), .b(input_2), .out(adder_1_out), .cout(adder_1_cout));  // open: cin
  assign and_1_out = input_1 & input_2;  // AND_Gate and_1, 8 bits wide
  assign or_1_out = input_1 | input_2;  // OR_Gate or_1, 8 bits wide
  assign xor_1_out = input_1 ^ input_2;  // XOR_Gate xor_1, 8 bits wide
  assign not_1_out = ~input_1;  // NOT_Gate not_1, 8 bits wide
  Multiplexer #(.select(2), .width(8)) multiplexer_1 (
    .in0(adder_1_out), .in1(and_1_out), .in2(or_1_out), .in3(xor_1_out), .out(multiplexer_1_out));  // open: sel
  Adder adder_2 (.a(not_1_out));  // open: b, out, cin, cout
  Multiplexer #(.width(8)) multiplexer_2 (.in0(multiplexer_1_out));  // open: in1, out, sel
  Multiplexer #(.select(2), .width(8)) multiplexer_3 (.in0(not_1_out));  // open: in1, in2, in3, out, sel
endmodule

module fifo (
  input  [31:0] input_data,
  input  res,
  input  assert_en,
  input  load_en,
  output [31:0] output_data
);

  wire clock_1_out, clock_2_out, clock_3_out, decoder_1_out0, decoder_1_out1, decoder_1_out2, decoder_1_out3,
       decoder_1_out4, decoder_1_out5, decoder_1_out6, decoder_1_out7, decoder_1_out8, decoder_1_out9,
       decoder_1_out10, decoder_1_out11, decoder_1_out12, decoder_1_out13, decoder_1_out14, decoder_1_out15,
       decoder_2_out0, decoder_2_out1, decoder_2_out2, decoder_2_out3, decoder_2_out4, decoder_2_out5,
       decoder_2_out6, decoder_2_out7, decoder_2_out8, decoder_2_out9, decoder_2_out10, decoder_2_out11,
       decoder_2_out12, decoder_2_out13, decoder_2_out14, decoder_2_out15;
  wire [3:0] assert_index_q, load_index_q;
  wire [31:0] register_1_q, register_2_q, register_3_q, register_4_q, register_5_q, register_6_q,
       register_7_q, register_8_q, register_9_q, register_10_q, register_11_q, register_12_q, register_13_q,
       register_14_q, register_15_q, register_16_q;

  Clock clock_1 (.out(clock_1_out));
  Counter #(.max('hf), .width(4)) assert_index (
    .up(1'b1), .count(assert_en), .clk(clock_1_out), .Q(assert_index_q));  // open: clr, load, D, carry
  Counter #(.max('hf), .width(4)) load_index (
    .clr(res), .up(1'b1), .count(load_en), .clk(clock_2_out), .Q(load_index_q));  // open: load, D, carry
  Clock clock_2 (.out(clock_2_out));
  Decoder #(.enable("false"), .select(4)) decoder_1 (
    .out0(decoder_1_out0), .out1(decoder_1_out1), .out2(decoder_1_out2), .out3(decoder_1_out3),
    .out4(decoder_1_out4), .out5(decoder_1_out5), .out6(decoder_1_out6), .out7(decoder_1_out7),
    .out8(decoder_1_out8), .out9(decoder_1_out9), .out10(decoder_1_out10), .out11(decoder_1_out11),
    .out12(decoder_1_out12), .out13(decoder_1_out13), .out14(decoder_1_out14), .out15(decoder_1_out15),
    .sel(load_index_q));
  Comparator #(.width(4)) comparator_1 (.a(load_index_q), .b(assert_index_q));  // open: gt, eq, lt
  Clock clock_3 (.out(clock_3_out));
  Register #(.width(32)) register_1 (
    .D(input_data), .en(decoder_1_out0), .clk(clock_3_out), .Q(register_1_q), .clr(res));
  Register #(.width(32)) register_2 (
    .D(input_data), .en(decoder_1_out1), .clk(clock_3_out), .Q(register_2_q), .clr(res));
  Register #(.width(32)) register_3 (
    .D(input_data), .en(decoder_1_out2), .clk(clock_3_out), .Q(register_3_q), .clr(res));
  Register #(.width(32)) register_4 (
    .D(input_data), .en(decoder_1_out3), .clk(clock_3_out), .Q(register_4_q), .clr(res));
  Register #(.width(32)) register_5 (
    .D(input_data), .en(decoder_1_out4), .clk(clock_3_out), .Q(register_5_q), .clr(res));
  Register #(.width(32)) register_6 (
    .D(input_data), .en(decoder_1_out5), .clk(clock_3_out), .Q(register_6_q), .clr(res));
  Register #(.width(32)) register_7 (
    .D(input_data), .en(decoder_1_out6), .clk(clock_3_out), .Q(register_7_q), .clr(res));
  Register #(.width(32)) register_8 (
    .D(input_data), .en(decoder_1_out7), .clk(clock_3_out), .Q(register_8_q), .clr(res));
  Register #(.width(32)) register_9 (
    .D(input_data), .en(decoder_1_out8), .clk(clock_3_out), .Q(register_9_q), .clr(res));
  Register #(.width(32)) register_10 (
    .D(input_data), .en(decoder_1_out9), .clk(clock_3_out), .Q(register_10_q), .clr(res));
  Register #(.width(32)) register_11 (
    .D(input_data), .en(decoder_1_out10), .clk(clock_3_out), .Q(register_11_q), .clr(res));
  Register #(.width(32)) register_12 (
    .D(input_data), .en(decoder_1_out11), .clk(clock_3_out), .Q(register_12_q), .clr(res));
  Register #(.width(32)) register_13 (
    .D(input_data), .en(decoder_1_out12), .clk(clock_3_out), .Q(register_13_q), .clr(res));
  Register #(.width(32)) register_14 (
    .D(input_data), .en(decoder_1_out13), .clk(clock_3_out), .Q(register_14_q), .clr(res));
  Register #(.width(32)) register_15 (
    .D(input_data), .en(decoder_1_out14), .clk(clock_3_out), .Q(register_15_q), .clr(res));
  Register #(.width(32)) register_16 (
    .D(input_data), .en(decoder_1_out15), .clk(clock_3_out), .Q(register_16_q), .clr(res));
  assign output_data = decoder_2_out0 ? register_1_q : 32'bz;  // Controlled_Buffer controlled_buffer_1
  assign output_data = decoder_2_out1 ? register_2_q : 32'bz;  // Controlled_Buffer controlled_buffer_2
  assign output_data = decoder_2_out2 ? register_3_q : 32'bz;  // Controlled_Buffer controlled_buffer_3
  assign output_data = decoder_2_out3 ? register_4_q : 32'bz;  // Controlled_Buffer controlled_buffer_4
  assign output_data = decoder_2_out4 ? register_5_q : 32'bz;  // Controlled_Buffer controlled_buffer_5
  assign output_data = decoder_2_out5 ? register_6_q : 32'bz;  // Controlled_Buffer controlled_buffer_6
  assign output_data = decoder_2_out6 ? register_7_q : 32'bz;  // Controlled_Buffer controlled_buffer_7
  assign output_data = decoder_2_out7 ? register_8_q : 32'bz;  // Controlled_Buffer controlled_buffer_8
  assign output_data = decoder_2_out8 ? register_9_q : 32'bz;  // Controlled_Buffer controlled_buffer_9
  assign output_data = decoder_2_out9 ? register_10_q : 32'bz;  // Controlled_Buffer controlled_buffer_10
  assign output_data = decoder_2_out10 ? register_11_q : 32'bz;  // Controlled_Buffer controlled_buffer_11
  assign output_data = decoder_2_out11 ? register_12_q : 32'bz;  // Controlled_Buffer controlled_buffer_12
  assign output_data = decoder_2_out12 ? register_13_q : 32'bz;  // Controlled_Buffer controlled_buffer_13
  assign output_data = decoder_2_out13 ? register_14_q : 32'bz;  // Controlled_Buffer controlled_buffer_14
  assign output_data = decoder_2_out14 ? register_15_q : 32'bz;  // Controlled_Buffer controlled_buffer_15
  assign output_data = decoder_2_out15 ? register_16_q : 32'bz;  // Controlled_Buffer controlled_buffer_16
  Decoder #(.enable("false"), .select(4)) decoder_2 (
    .out0(decoder_2_out0), .out1(decoder_2_out1), .out2(decoder_2_out2), .out3(decoder_2_out3),
    .out4(decoder_2_out4), .out5(decoder_2_out5), .out6(decoder_2_out6), .out7(decoder_2_out7),
    .out8(decoder_2_out8), .out9(decoder_2_out9), .out10(decoder_2_out10), .out11(decoder_2_out11),
    .out12(decoder_2_out12), .out13(decoder_2_out13), .out14(decoder_2_out14), .out15(decoder_2_out15),
    .sel(assert_index_q));
endmodule
